# Fritzing sketch Final_Project_IOT_Temp_Humi_LCD_Schema (saved by Fritzing 0.9.9b)
breadboards: 2

parts:
  Mod1 = Raspberry Pi 4B
  LCD1 = LCD screen
  U1 = POT [package=3362u]
  RHT1 = Humidity and Temperature Sensor RHT03
  R1 = Resistor [tolerance=±5% resistance=1k package="0603 [SMD]"]

nets:
  5V: Mod1.5V, LCD1.VDD, LCD1.LED+, U1.E, RHT1.Vcc, R1.Pin_0
  GND: Mod1.GND, LCD1.VSS, LCD1.R/W, LCD1.LED-, U1.A, RHT1.GND_2
  N1: Mod1.GPIO4, RHT1.Data-signal, R1.Pin_1
  N2: Mod1.GPIO17, LCD1.DB5
  N3: Mod1.GPIO18, LCD1.DB6
  N4: Mod1.GPIO22, LCD1.DB7
  N5: Mod1.GPIO23, LCD1.DB4
  N6: Mod1.GPIO24, LCD1.E
  N7: Mod1.GPIO25, LCD1.RS
  N8: LCD1.V0, U1.S
